// Logisim project harvard.circ as structural Verilog: 1 circuit, main circuit main
module main (
);

  wire cdm_8_mark5_1_data_inst, cdm_8_mark5_1_mem_cycle, cdm_8_mark5_1_mem_read, clock, decoder_1_out0,
       decoder_1_out1, not_1_out;
  wire [7:0] cdm_8_mark5_1_addr, cdm_8_mark5_1_data_out, cdm_8_mark5_1_pc, cdm_8_mark5_1_ps,
       cdm_8_mark5_1_r0, cdm_8_mark5_1_r1, cdm_8_mark5_1_r2, cdm_8_mark5_1_r3, cdm_8_mark5_1_sp,
       controlled_buffer_1_out, controlled_buffer_2_out;

  // Probe on cdm_8_mark5_1_r0
  // Probe on cdm_8_mark5_1_r1
  Clock clock_1 (.out(clock));
  // Probe on cdm_8_mark5_1_r3
  // Probe on cdm_8_mark5_1_r2
  // Probe on cdm_8_mark5_1_pc
  // Probe on cdm_8_mark5_1_ps
  // Probe on cdm_8_mark5_1_sp
  CdM_8_mark5 cdm_8_mark5_1 (
    .clock(clock), .addr(cdm_8_mark5_1_addr), .mem_read(cdm_8_mark5_1_mem_read),
    .mem_cycle(cdm_8_mark5_1_mem_cycle), .data_inst(cdm_8_mark5_1_data_inst),
    .data_out(cdm_8_mark5_1_data_out), .data_in(controlled_buffer_1_out), .r0(cdm_8_mark5_1_r0),
    .r1(cdm_8_mark5_1_r1), .r2(cdm_8_mark5_1_r2), .r3(cdm_8_mark5_1_r3), .PC(cdm_8_mark5_1_pc),
    .SP(cdm_8_mark5_1_sp), .PS(cdm_8_mark5_1_ps));  // open: IAck, IRQ, vec
  assign controlled_buffer_1_out = cdm_8_mark5_1_mem_read ? controlled_buffer_2_out : 8'bz;  // Controlled_Buffer controlled_buffer_1
  Decoder #(.disabled(0)) decoder_1 (
    .out0(decoder_1_out0), .out1(decoder_1_out1), .sel(cdm_8_mark5_1_data_inst), .en(cdm_8_mark5_1_mem_cycle));
  not not_1 (not_1_out, cdm_8_mark5_1_mem_read);
  assign controlled_buffer_2_out = not_1_out ? cdm_8_mark5_1_data_out : 8'bz;  // Controlled_Buffer controlled_buffer_2
  ROM rom_1 (.addr(cdm_8_mark5_1_addr), .data(controlled_buffer_2_out), .sel(decoder_1_out0));
  RAM ram_1 (
    .addr(cdm_8_mark5_1_addr), .data(controlled_buffer_2_out), .sel(decoder_1_out1), .clk(clock),
    .ld(cdm_8_mark5_1_mem_read));  // open: clr

  // Notes on the sheet:
  //   contents of rom_1 (hex, n*v repeats v):
  //   d0 f d1 1a 14 d3 0 ac d4
endmodule
