// Logisim project adders.circ as structural Verilog: 6 circuits, main circuit main
module main (
  input  Carry_in__Cin0,
  input  [2:0] A,
  input  [2:0] B,
  output [2:0] Result,
  output Result_carry_out__CoutR
);

  wire Full_adder_1_coutr, Full_adder_2_coutr;

  Full_Adder Full_adder_1 (.Cout1(A[0]), .in_2(B[0]), .in_3(Carry_in__Cin0), .CoutR(Full_adder_1_coutr), .R(Result[0]));
  Full_Adder Full_adder_2 (
    .Cout1(A[1]), .in_2(B[1]), .in_3(Full_adder_1_coutr), .CoutR(Full_adder_2_coutr), .R(Result[1]));
  Full_Adder Full_adder_3 (
    .Cout1(A[2]), .in_2(B[2]), .in_3(Full_adder_2_coutr), .CoutR(Result_carry_out__CoutR), .R(Result[2]));
endmodule

module _2 (
  input  A,
  input  B,
  output A___B____2,
  output Carry_bit
);

  xor xor_1 (Carry_bit, A, B);
  and and_1 (A___B____2, A, B);

  // Notes on the sheet:
  //   2 bit half adder
endmodule

module Full_Adder (
  input  Cout1,
  input  in_2,
  input  in_3,
  output CoutR,
  output R
);

  wire _2_2_a___b____2, _2_a___b____2, _2_carry_bit;

  _2 _2 (.A(Cout1), .B(in_2), .A___B____2(_2_a___b____2), .Carry_bit(_2_carry_bit));
  _2 _2_2 (.A(_2_carry_bit), .B(in_3), .A___B____2(_2_2_a___b____2), .Carry_bit(R));
  or or_1 (CoutR, _2_a___b____2, _2_2_a___b____2);

  // Notes on the sheet:
  //   Cout2
endmodule

module Repeated_sum (
  input  Carry_in__Cin0,
  input  [2:0] A,
  input  [2:0] B,
  output Result_carry_out__CoutR,
  output [2:0] Result
);

  wire [1:0] _3_bits_Full_Adder_coutr;

  Full_adder_3_bits _3_bits_Full_Adder (
    .Cout1(A), .in_2(B), .in_3({_3_bits_Full_Adder_coutr, Carry_in__Cin0}),
    .CoutR({Result_carry_out__CoutR, _3_bits_Full_Adder_coutr}), .R(Result));
endmodule

module Full_adder_3_bits (
  input  [2:0] Cout1,
  input  [2:0] in_2,
  input  [2:0] in_3,
  output [2:0] CoutR,
  output [2:0] R
);

  wire [2:0] n2_3_bits_1_a___b____2, n2_3_bits_1_carry_bit, n2_3_bits_2_a___b____2;

  _2_3_bits u_2_3_bits_1 (.A(Cout1), .B(in_2), .A___B____2(n2_3_bits_1_a___b____2), .Carry_bit(n2_3_bits_1_carry_bit));
  _2_3_bits u_2_3_bits_2 (.A(n2_3_bits_1_carry_bit), .B(in_3), .A___B____2(n2_3_bits_2_a___b____2), .Carry_bit(R));
  assign CoutR = n2_3_bits_1_a___b____2 | n2_3_bits_2_a___b____2;  // OR_Gate or_1, 3 bits wide

  // Notes on the sheet:
  //   Cout2
endmodule

module _2_3_bits (
  input  [2:0] A,
  input  [2:0] B,
  output [2:0] A___B____2,
  output [2:0] Carry_bit
);

  assign Carry_bit = A ^ B;  // XOR_Gate xor_1, 3 bits wide
  assign A___B____2 = A & B;  // AND_Gate and_1, 3 bits wide

  // Notes on the sheet:
  //   2 bit half adder
endmodule
