// Logisim project cdm8e_test.circ as structural Verilog: 1 circuit, main circuit main
module main (
  input  [2:0] in_1
);

  wire and_1_out, and_2_out, and_3_out, button_1_out, cdm_8_mark5_1_data_inst, cdm_8_mark5_1_iack,
       cdm_8_mark5_1_mem_cycle, cdm_8_mark5_1_mem_read, clk, decoder_1_out0, decoder_1_out1, not_1_out,
       or_1_out, zero_periph;
  wire [0:0] button_2_out;
  wire [6:0] bit_extender_1_out, keyboard_1_data;
  wire [7:0] bit_extender_2_out, cdm_8_mark5_1_data_out, cdm_8_mark5_1_ps, cdm_8_mark5_1_r0,
       cdm_8_mark5_1_r1, cdm_8_mark5_1_r2, cdm_8_mark5_1_r3, cdm_8_mark5_1_sp, controlled_buffer_1_out,
       controlled_buffer_2_out;
  wire [15:0] cdm_8_mark5_1_addr, cdm_8_mark5_1_pc;

  Button button_1 (.out(button_1_out));
  Button button_2 (.out(button_2_out[0]));
  Clock clock_1 (.out(clk));
  or or_1 (or_1_out, button_1_out, button_2_out[0]);
  LED led_1 (.in(cdm_8_mark5_1_iack));
  // Probe on cdm_8_mark5_1_r0
  // Probe on cdm_8_mark5_1_r1
  // Probe on cdm_8_mark5_1_r2
  // Probe on cdm_8_mark5_1_ps
  // Probe on cdm_8_mark5_1_r3
  // Probe on cdm_8_mark5_1_pc
  // Probe on cdm_8_mark5_1_sp
  Decoder #(.disabled(0)) decoder_1 (
    .out0(decoder_1_out0), .out1(decoder_1_out1), .sel(cdm_8_mark5_1_data_inst), .en(cdm_8_mark5_1_mem_cycle));
  CdM_8_mark5 cdm_8_mark5_1 (
    .clock(clk), .addr(cdm_8_mark5_1_addr), .mem_read(cdm_8_mark5_1_mem_read),
    .mem_cycle(cdm_8_mark5_1_mem_cycle), .data_inst(cdm_8_mark5_1_data_inst),
    .data_out(cdm_8_mark5_1_data_out), .data_in(controlled_buffer_2_out), .r0(cdm_8_mark5_1_r0),
    .r1(cdm_8_mark5_1_r1), .r2(cdm_8_mark5_1_r2), .r3(cdm_8_mark5_1_r3), .PC(cdm_8_mark5_1_pc),
    .SP(cdm_8_mark5_1_sp), .PS(cdm_8_mark5_1_ps), .IAck(cdm_8_mark5_1_iack), .IRQ(or_1_out),
    .vec({2'b00, button_2_out[0]}));  // open: halted
  not not_1 (not_1_out, cdm_8_mark5_1_mem_read);
  assign controlled_buffer_1_out = not_1_out ? cdm_8_mark5_1_data_out : 8'bz;  // Controlled_Buffer controlled_buffer_1
  assign controlled_buffer_2_out = cdm_8_mark5_1_mem_read ? controlled_buffer_1_out : 8'bz;  // Controlled_Buffer controlled_buffer_2
  and and_1 (and_1_out, ~zero_periph, decoder_1_out1);  // AND_Gate
  // Probe on controlled_buffer_1_out
  Bit_Extender #(.out_width(7), .\type ("sign")) bit_extender_1 (
    .in(controlled_buffer_1_out), .out(bit_extender_1_out));
  TTY tty_1 (.data(bit_extender_1_out), .clk(clk), .we(and_2_out));  // open: clr
  and and_2 (and_2_out, decoder_1_out1, ~cdm_8_mark5_1_mem_read, zero_periph);  // AND_Gate
  and and_3 (and_3_out, decoder_1_out1, cdm_8_mark5_1_mem_read, zero_periph);
  Comparator #(.width(16)) comparator_1 (.a(cdm_8_mark5_1_addr), .b({16{1'b0}}), .eq(zero_periph));  // open: gt, lt
  RAM ram_1 (
    .addr(cdm_8_mark5_1_addr[7:0]), .data(controlled_buffer_1_out), .sel(and_1_out), .clk(clk),
    .ld(cdm_8_mark5_1_mem_read));  // open: clr
  ROM #(.addrWidth(16)) rom_1 (.addr(cdm_8_mark5_1_addr), .data(controlled_buffer_1_out), .sel(decoder_1_out0));
  Keyboard #(.trigger("falling")) keyboard_1 (.clk(clk), .re(and_3_out), .data(keyboard_1_data));  // open: clr, avail
  assign controlled_buffer_1_out = and_3_out ? bit_extender_2_out : 8'bz;  // Controlled_Buffer controlled_buffer_3
  assign bit_extender_2_out = {{1{1'b0}}, keyboard_1_data};  // Bit_Extender bit_extender_2

  // Notes on the sheet:
  //   RAM
  //   ROM
endmodule
