// Logisim project priority_encoder.circ as structural Verilog: 1 circuit, main circuit main
module main (
  input  [7:0] in_1,
  input  Enable_input,
  output out_3,
  output [2:0] out_4,
  output out_5
);

  Priority_Encoder priority_encoder_1 (
    .in0(in_1[0]), .in1(in_1[1]), .in2(in_1[2]), .in3(in_1[3]), .in4(in_1[4]), .in5(in_1[5]), .in6(in_1[6]),
    .in7(in_1[7]), .out(out_4), .en_in(Enable_input), .gs(out_5), .en_out(out_3));

  // Notes on the sheet:
  //   Data-inputs
  //   Priority encoder
  //   1 when ALL data-inputs are 0
  //   1 when anyone of inputs is 1
  //   Show numver of highest 1 input
endmodule
