// Logisim project harvard IO improved.circ as structural Verilog: 1 circuit, main circuit main
module main (
  input  [7:0] in_1
);

  wire and_3_out, button_1_out, cdm_8_mark5_1_data_inst, clock, code, comparator_1_lt, comparator_2_eq, data,
       decoder_2_out0, decoder_2_out1, in_out, IOsel, mem, not_1_out, not_2_out, not_3_out, not_4_out,
       not_5_out, not_6_out, or_1_out, RAM;
  wire [7:0] addr, bus, cdm_8_mark5_1_data_out, cdm_8_mark5_1_pc, cdm_8_mark5_1_ps, cdm_8_mark5_1_r0,
       cdm_8_mark5_1_r1, cdm_8_mark5_1_r2, cdm_8_mark5_1_r3, cdm_8_mark5_1_sp, controlled_buffer_2_out,
       controlled_buffer_3_out, register_1_q;

  // Probe on cdm_8_mark5_1_r1
  // Probe on cdm_8_mark5_1_r0
  Clock clock_1 (.out(clock));
  and and_1 (IOsel, not_1_out, clock, data);
  // Probe on cdm_8_mark5_1_r3
  // Probe on cdm_8_mark5_1_r2
  // Probe on cdm_8_mark5_1_pc
  not not_1 (not_1_out, comparator_1_lt);
  not not_2 (not_2_out, not_2_out);
  // Probe on cdm_8_mark5_1_sp
  // Probe on cdm_8_mark5_1_ps
  CdM_8_mark5 cdm_8_mark5_1 (
    .clock(clock), .addr(addr), .mem_read(in_out), .mem_cycle(mem), .data_inst(cdm_8_mark5_1_data_inst),
    .data_out(cdm_8_mark5_1_data_out), .data_in(controlled_buffer_2_out), .r0(cdm_8_mark5_1_r0),
    .r1(cdm_8_mark5_1_r1), .r2(cdm_8_mark5_1_r2), .r3(cdm_8_mark5_1_r3), .PC(cdm_8_mark5_1_pc),
    .SP(cdm_8_mark5_1_sp), .PS(cdm_8_mark5_1_ps));  // open: IAck, IRQ, vec
  assign bus = not_3_out ? cdm_8_mark5_1_data_out : 8'bz;  // Controlled_Buffer controlled_buffer_1
  not not_3 (not_3_out, in_out);
  and and_2 (RAM, comparator_1_lt, data);
  Button button_1 (.out(button_1_out));
  Decoder #(.disabled(0)) decoder_1 (.out0(code), .out1(data), .sel(cdm_8_mark5_1_data_inst), .en(mem));
  assign controlled_buffer_2_out = in_out ? bus : 8'bz;  // Controlled_Buffer controlled_buffer_2
  not not_4 (not_4_out, button_1_out);
  assign controlled_buffer_3_out = not_4_out ? bus : 8'bz;  // Controlled_Buffer controlled_buffer_3
  assign controlled_buffer_3_out = button_1_out ? in_1 : 8'bz;  // Controlled_Buffer controlled_buffer_4
  not not_5 (not_5_out, not_6_out);
  not not_6 (not_6_out, button_1_out);
  // Probe on addr
  assign bus = decoder_2_out1 ? register_1_q : 8'bz;  // Controlled_Buffer controlled_buffer_5
  Register register_1 (.D(controlled_buffer_3_out), .Q(register_1_q), .clk(or_1_out));  // open: en, clr
  or or_1 (or_1_out, not_5_out, decoder_2_out0);
  Comparator #(.mode("unsigned")) comparator_1 (.a(addr), .b(8'hf0), .lt(comparator_1_lt));  // open: gt, eq
  Decoder #(.disabled(0)) decoder_2 (.out0(decoder_2_out0), .out1(decoder_2_out1), .sel(in_out), .en(and_3_out));
  // Probe on bus
  ROM rom_1 (.addr(addr), .data(bus), .sel(code));
  RAM ram_1 (.addr(addr), .data(bus), .sel(RAM), .clk(clock), .ld(in_out));  // open: clr
  Comparator comparator_2 (.a(addr), .b(8'hf0), .eq(comparator_2_eq));  // open: gt, lt
  and and_3 (and_3_out, comparator_2_eq, IOsel);

  // Other names for the same wires on the sheet: IOaddr[7:0] = addr; IOdata[7:0] = bus; rd_wr = in_out

  // Notes on the sheet:
  //   Structure of I/O bus
  //   Cell 0xf0
  //   Harvard Architecture
  //   Minimal IO cell address
  //   contents of rom_1 (hex, n*v repeats v):
  //   cc f0 d0 f0 a e1 a b2 ee 4 2a a2 d4
endmodule
