// Logisim project harvard IO.circ as structural Verilog: 1 circuit, main circuit main
module main (
  input  [7:0] A,
  input  [7:0] B
);

  wire A_out, and_1_out, and_2_out, and_3_out, and_4_out, B_out, cdm_8_mark5_1_data_inst,
       cdm_8_mark5_1_mem_cycle, cdm_8_mark5_1_mem_read, clock, decoder_1_out0, decoder_1_out1, not_1_out,
       or_1_out, or_2_out;
  wire [7:0] cdm_8_mark5_1_addr, cdm_8_mark5_1_data_out, cdm_8_mark5_1_pc, cdm_8_mark5_1_ps,
       cdm_8_mark5_1_r0, cdm_8_mark5_1_r1, cdm_8_mark5_1_r2, cdm_8_mark5_1_r3, cdm_8_mark5_1_sp,
       controlled_buffer_1_out, controlled_buffer_2_out, controlled_buffer_3_out, multiplexer_1_out,
       multiplexer_2_out;

  // Probe on cdm_8_mark5_1_r1
  // Probe on cdm_8_mark5_1_r0
  Clock clock_1 (.out(clock));
  // Probe on cdm_8_mark5_1_r2
  // Probe on cdm_8_mark5_1_r3
  // Probe on cdm_8_mark5_1_pc
  // Probe on cdm_8_mark5_1_ps
  and and_1 (and_1_out, cdm_8_mark5_1_mem_cycle, ~or_2_out);  // AND_Gate
  // Probe on cdm_8_mark5_1_sp
  CdM_8_mark5 cdm_8_mark5_1 (
    .clock(clock), .addr(cdm_8_mark5_1_addr), .mem_read(cdm_8_mark5_1_mem_read),
    .mem_cycle(cdm_8_mark5_1_mem_cycle), .data_inst(cdm_8_mark5_1_data_inst),
    .data_out(cdm_8_mark5_1_data_out), .data_in(controlled_buffer_1_out), .r0(cdm_8_mark5_1_r0),
    .r1(cdm_8_mark5_1_r1), .r2(cdm_8_mark5_1_r2), .r3(cdm_8_mark5_1_r3), .PC(cdm_8_mark5_1_pc),
    .SP(cdm_8_mark5_1_sp), .PS(cdm_8_mark5_1_ps));  // open: IAck, IRQ, vec
  assign controlled_buffer_1_out = and_2_out ? controlled_buffer_2_out : 8'bz;  // Controlled_Buffer controlled_buffer_1
  and and_2 (and_2_out, cdm_8_mark5_1_mem_read, ~or_2_out);  // AND_Gate
  Decoder #(.disabled(0)) decoder_1 (
    .out0(decoder_1_out0), .out1(decoder_1_out1), .sel(cdm_8_mark5_1_data_inst), .en(and_1_out));
  not not_1 (not_1_out, or_2_out);
  assign controlled_buffer_2_out = and_3_out ? cdm_8_mark5_1_data_out : 8'bz;  // Controlled_Buffer controlled_buffer_2
  and and_3 (and_3_out, ~cdm_8_mark5_1_mem_read, ~or_2_out);  // AND_Gate
  Button u_A (.out(A_out));
  assign controlled_buffer_3_out = not_1_out ? cdm_8_mark5_1_addr : 8'bz;  // Controlled_Buffer controlled_buffer_3
  assign controlled_buffer_3_out = or_2_out ? multiplexer_1_out : 8'bz;  // Controlled_Buffer controlled_buffer_4
  Multiplexer #(.width(8), .disabled(0), .enable("false")) multiplexer_1 (
    .in0(8'hf1), .in1(8'hf0), .out(multiplexer_1_out), .sel(A_out));
  and and_4 (and_4_out, cdm_8_mark5_1_mem_read, ~or_2_out);  // AND_Gate
  or or_1 (or_1_out, decoder_1_out1, or_2_out);
  or or_2 (or_2_out, A_out, B_out);
  ROM rom_1 (.addr(controlled_buffer_3_out), .data(controlled_buffer_2_out), .sel(decoder_1_out0));
  RAM ram_1 (
    .addr(controlled_buffer_3_out), .data(controlled_buffer_2_out), .sel(or_1_out), .clk(clock),
    .ld(and_4_out));  // open: clr
  assign controlled_buffer_2_out = or_2_out ? multiplexer_2_out : 8'bz;  // Controlled_Buffer controlled_buffer_5
  Multiplexer #(.width(8), .disabled(0), .enable("false")) multiplexer_2 (
    .in0(A), .in1(B), .out(multiplexer_2_out), .sel(B_out));
  Button u_B (.out(B_out));

  // Notes on the sheet:
  //   contents of rom_1 (hex, n*v repeats v):
  //   cc f0 d0 f0 d1 f1 a e1 c b2 ee 6 f e1 12 b7 ee c 1b d0 0 a3 d4
endmodule
